# Fritzing sketch Weevle_Soldering (saved by Fritzing 0.9.6b)
breadboards: 1

parts:
  R1 = PHOTOCELL [package=photocell-kit]
  3V_Coincell = Battery Holders [package=battcom_20mm_pth]
  R2 = Resistor [tolerance=±5% power=0.25 resistance=47k package=THT]
  R3 = Resistor [tolerance=±5% resistance=220 package="0402 [SMD]"]
  R4 = Resistor [tolerance=±5% resistance=220 package="0402 [SMD]"]
  Red_LED = smd LED [color="Red (633nm)" package="0805 [SMD]"]
  Q1 = NPN-Transistor [package="SOT-23 [SMD]"]
  Red_LED_2 = smd LED [color="Red (633nm)" package="0805 [SMD]"]

nets:
  N1: R1.P$1, R2.Pin_0, Q1.0
  N2: R1.P$2, 3V_Coincell.-, Q1.2
  N3: 3V_Coincell.+, R2.Pin_1, Red_LED.anode, Red_LED_2.anode
  N4: R3.Pin_0, Red_LED_2.cathode
  N5: R3.Pin_1, R4.Pin_1, Q1.1
  N6: R4.Pin_0, Red_LED.cathode
