# Fritzing sketch BasicLEDPlayground (saved by Fritzing 0.9.10b)
breadboards: 1

parts:
  Part1 = Arduino Uno (Rev3)
  LED1 = RGB LED - (4 legs) [package="5 mm [THT]"]
  LED2 = LED - 5mm [color="Yellow (574nm)" current=0.030 package="5 mm [THT]"]
  LED3 = LED - 5mm [color="White (6500K)" current=0.030 package="5 mm [THT]"]
  LED4 = LED - 5mm [color="Red (635nm)" current=0.030 package="5 mm [THT]"]
  LED5 = LED - 5mm [color="Green (560nm)" current=0.030 package="5 mm [THT]"]
  LED6 = LED - 5mm [color="Blue (430nm)" current=0.030 package="5 mm [THT]"]
  R1 = Resistor [tolerance=±5% resistance=330 package="2010 [SMD]"]
  R2 = Resistor [tolerance=±5% resistance=330 package="2010 [SMD]"]
  R3 = Resistor [tolerance=±5% resistance=330 package="2010 [SMD]"]
  R4 = Resistor [tolerance=±5% resistance=330 package="2010 [SMD]"]
  R5 = Resistor [tolerance=±5% resistance=330 package="2010 [SMD]"]
  R6 = Resistor [tolerance=±5% resistance=330 package="2010 [SMD]"]
  R7 = Resistor [tolerance=±5% resistance=330 package="2010 [SMD]"]
  R8 = Resistor [tolerance=±5% resistance=330 package="2010 [SMD]"]

nets:
  N1: Part1.D12/MISO, R1.Pin_0
  N2: Part1.D13/SCK, R2.Pin_0
  N3: Part1.GND, LED1.common_anode, LED2.cathode, LED3.cathode, LED4.cathode, LED5.cathode, LED6.cathode
  N4: LED1.red_cathode, R6.Pin_1
  N5: LED1.green_cathode, R7.Pin_1
  N6: LED1.blue_cathode, R8.Pin_1
  N7: LED2.anode, R1.Pin_1
  N8: LED3.anode, R2.Pin_1
  N9: LED4.anode, R3.Pin_1
  N10: LED5.anode, R4.Pin_1
  N11: LED6.anode, R5.Pin_1
